# Fritzing sketch Motordroid1 (saved by Fritzing 0.8.7b)

parts:
  Parte1 = Arduino Mega 2560 (Rev3)  # not connected
  Parte2 = Arduino Motor Shield (Rev3)
  M2 = DC Motor
  Power_plug2 = Power plug  # not connected
  VCC2 = Battery block 9V  # not connected
  M3 = DC Motor
  Parte3 = Arduino Motor Shield (Rev3)
  M4 = DC Motor
  M5 = DC Motor
  VCC3 = Battery block 9V

nets:
  N1: Parte2.B-, M3.pin_2
  N2: Parte2.B+, M3.pin_1
  N3: Parte2.A-, M2.pin_2
  N4: Parte2.A+, M2.pin_1
  N5: Parte3.GND, VCC3.-
  N6: Parte3.B-, M4.pin_2
  N7: Parte3.B+, M4.pin_1
  N8: Parte3.A-, M5.pin_2
  N9: Parte3.A+, M5.pin_1
  N10: Parte3.VMOT, VCC3.+
