# Fritzing sketch Motordroid2.1 (saved by Fritzing 0.8.7b)
breadboards: 1

parts:
  LED1 = LED - 5mm [color="Blue (470nm)" package="5 mm [THT]"]
  LED2 = LED - 5mm [color="Blue (470nm)" package="5 mm [THT]"]
  Parte1 = Arduino Mega 2560 (Rev3)
  R1 = Resistor [tolerance=±5% resistance=1k package=THT]

nets:
  N1: LED1.cathode, LED2.cathode, R1.Pin_1
  N2: LED1.anode, LED2.anode, Parte1.D47
  N3: Parte1.GND, R1.Pin_0
