# Fritzing sketch Motordroid2 (saved by Fritzing 0.8.7b)
breadboards: 1

parts:
  LED1 = LED - 5mm [color="Blue (470nm)" package="5 mm [THT]"]
  LED2 = LED - 5mm [color="Blue (470nm)" package="5 mm [THT]"]
  Parte1 = Arduino Mega 2560 (Rev3)
  R1 = Resistor [tolerance=±5% resistance=1k package=THT]
  LED3 = LED - 5mm [color="White (4500K)" package="5 mm [THT]"]
  LED4 = LED - 5mm [color="White (4500K)" package="5 mm [THT]"]
  LED5 = LED - 5mm [color="Orange (620nm)" package="5 mm [THT]"]
  LED6 = LED - 5mm [color="Orange (620nm)" package="5 mm [THT]"]
  LED7 = LED - 5mm [color="Orange (620nm)" package="5 mm [THT]"]
  LED8 = LED - 5mm [color="Orange (620nm)" package="5 mm [THT]"]
  LED9 = LED - 5mm [color="White (4500K)" package="5 mm [THT]"]
  LED10 = LED - 5mm [color="White (4500K)" package="5 mm [THT]"]
  LED11 = LED - 5mm [color="Red (635nm)" package="5 mm [THT]"]
  LED12 = LED - 5mm [color="Red (635nm)" package="5 mm [THT]"]
  R2 = Resistor [tolerance=±5% resistance=1k package=THT]
  R3 = Resistor [tolerance=±5% resistance=1k package=THT]
  R4 = Resistor [tolerance=±5% resistance=1k package=THT]
  R5 = Resistor [tolerance=±5% resistance=1k package=THT]
  R6 = Resistor [tolerance=±5% resistance=220 package=THT]

nets:
  N1: LED1.cathode, LED2.cathode, R4.Pin_0
  N2: LED1.anode, LED2.anode, Parte1.D47
  N3: Parte1.D46, LED3.anode, LED4.anode
  N4: Parte1.D48, LED5.anode, LED7.anode
  N5: Parte1.D49, LED6.anode, LED8.anode
  N6: Parte1.D50, LED11.anode, LED12.anode
  N7: Parte1.D51, LED9.anode, LED10.anode
  N8: Parte1.GND, R1.Pin_0, R2.Pin_0, R3.Pin_0, R4.Pin_1, R5.Pin_1, R6.Pin_1
  N9: R1.Pin_1, LED11.cathode, LED12.cathode
  N10: LED3.cathode, R5.Pin_0
  N11: LED5.cathode, LED7.cathode, R2.Pin_1
  N12: LED6.cathode, LED8.cathode, R3.Pin_1
  N13: LED9.cathode, LED10.cathode, R6.Pin_0
