# Fritzing sketch Motordroid3 (saved by Fritzing 0.8.7b)
breadboards: 1

parts:
  Line_Tracker1 = Line Tracker
  Line_Tracker2 = Line Tracker
  Parte1 = Arduino Mega 2560 (Rev3)
  Parte3 = Bluetooth Mate Silver

nets:
  N1: Line_Tracker1.OUT, Parte1.A15
  VIN: Line_Tracker1.Vin, Line_Tracker2.Vin, Parte1.5V, Parte3.VCC
  GND: Line_Tracker1.GND, Line_Tracker2.GND, Parte1.GND, Parte3.GND
  N2: Line_Tracker2.OUT, Parte1.A14
  N3: Parte1.D15/RX3, Parte3.RX_5V
  N4: Parte1.D14/TX3, Parte3.RTS_5V

custom parts:
  Line Tracker: Line Tracker V3 from DFRobot
