# Fritzing sketch Motordroid4 (saved by Fritzing 0.8.7b)
breadboards: 2

parts:
  Parte1 = Arduino Mega 2560 (Rev3)
  C1 = Electrolytic Capacitor [capacitance=1µF package="100 mil [THT, electrolytic]"]
  J2 = Basic Servo
  J3 = Basic Servo
  Parte2 = SRF05 Ultrasonic Rangefinder
  LED1 = LED - 5mm [color="Red (633nm)" package="5 mm [THT]"]
  Parte3 = Arduino Motor Shield (Rev3)  # not connected

nets:
  N1: Parte1.A8, J3.pulse
  N2: Parte1.A9, J2.pulse
  VCC: Parte1.5V, C1.-, J2.vcc, J3.vcc, Parte2.VCC
  N3: Parte1.D22, Parte2.Echo
  N4: Parte1.D23, Parte2.Trig
  N5: Parte1.D30, LED1.anode
  N6: Parte1.D31, LED1.cathode
  GND: Parte1.GND, C1.+, J2.gnd, J3.gnd, Parte2.GND

notes:
  Láser
