# Fritzing sketch SimpleBotonLed (saved by Fritzing 0.8.7b)
breadboards: 1

parts:
  R1 = Resistor [tolerance=±5% resistance=1k package=THT]
  S1 = Pushbutton [package="[THT]"]
  LED1 = LED - 5mm [color="Red (633nm)" package="5 mm [THT]"]
  Parte1 = Arduino Uno (Rev3)

nets:
  N1: R1.Pin_0, S1.Pin_3, S1.Pin_4, Parte1.GND
  N2: R1.Pin_1, LED1.cathode
  N3: S1.Pin_1, S1.Pin_2, Parte1.D2
  N4: LED1.anode, Parte1.D12/MISO
