# Fritzing sketch IntermitenteLedBoton (saved by Fritzing 0.8.7b)
breadboards: 1

parts:
  S2 = Pushbutton [package="[THT]"]
  LED1 = LED - 5mm [color="Yellow (595nm)" package="5 mm [THT]"]
  LED2 = LED - 5mm [color="Yellow (595nm)" package="5 mm [THT]"]
  S1 = Pushbutton [package="[THT]"]
  R1 = Resistor [tolerance=±5% resistance=1k package=THT]
  R2 = Resistor [tolerance=±5% resistance=1k package=THT]
  Parte2 = Arduino Uno (Rev3)

nets:
  N1: S2.Pin_1, S2.Pin_2, S1.Pin_1, S1.Pin_2, R2.Pin_0, Parte2.GND
  N2: S2.Pin_3, S2.Pin_4, Parte2.D1/TX
  N3: LED1.cathode, R1.Pin_1
  N4: LED1.anode, Parte2.D12/MISO
  N5: LED2.anode, Parte2.D11_PWM/MOSI
  N6: S1.Pin_3, S1.Pin_4, Parte2.D2
