# Fritzing sketch SensorLineaBlanca (saved by Fritzing 0.8.7b)

parts:
  Parte1 = Arduino Uno (Rev3)
  Line_Tracker1 = Line Tracker
  LED1 = LED - 5mm [color="Green (565nm)" package="5 mm [THT]"]

nets:
  N1: Parte1.A0, Line_Tracker1.OUT
  GND: Parte1.GND, Line_Tracker1.GND, LED1.anode
  N2: Parte1.AREF, LED1.cathode
  5V: Parte1.5V, Line_Tracker1.Vin

custom parts:
  Line Tracker: Line Tracker V3 from DFRobot
