# Fritzing sketch DistanciaUltrasonido (saved by Fritzing 0.8.7b)

parts:
  Parte1 = Arduino Uno (Rev3)
  Parte2 = SRF05 Ultrasonic Rangefinder

nets:
  N1: Parte1.D10_PWM/SS, Parte2.Echo
  N2: Parte1.D11_PWM/MOSI, Parte2.Trig
  GND: Parte1.GND, Parte2.GND
  5V: Parte1.5V, Parte2.VCC
