# Fritzing sketch BiRuedaAutonomo (saved by Fritzing 0.8.7b)

parts:
  Parte2 = Arduino Motor Shield (Rev3)
  M1 = DC Motor
  M2 = DC Motor
  VCC1 = Battery block 9V  # not connected
  Power_plug1 = Power plug  # not connected
  Parte3 = Arduino Uno (Rev3)  # not connected

nets:
  N1: Parte2.B-, M1.pin_2
  N2: Parte2.B+, M1.pin_1
  N3: Parte2.A-, M2.pin_2
  N4: Parte2.A+, M2.pin_1
