# Fritzing sketch MovimientoServomotor (saved by Fritzing 0.8.7b)

parts:
  J1 = Basic Servo
  Parte2 = Arduino Uno (Rev3)  # not connected
  Parte3 = Arduino Motor Shield (Rev3)

nets:
  GND: J1.gnd, Parte3.GND
  N1: J1.pulse, Parte3.D2
