# Fritzing sketch ConfiguraciónBluetooth (saved by Fritzing 0.8.7b)
breadboards: 1

parts:
  Parte2 = Bluetooth Mate Silver
  Parte3 = Arduino Uno (Rev3)

nets:
  N1: Parte2.RX_5V, Parte3.D1/TX
  N2: Parte2.TX_5V, Parte3.D0/RX
  VCC: Parte2.VCC, Parte3.5V
  GND: Parte2.GND, Parte3.GND
