# Fritzing sketch BiRuedaBluetooth (saved by Fritzing 0.8.7b)

parts:
  Parte1 = Arduino Mega 2560 (Rev3)
  Parte2 = Arduino Motor Shield (Rev3)
  M1 = DC Motor
  M2 = DC Motor
  VCC1 = Battery block 9V  # not connected
  Power_plug1 = Power plug  # not connected
  Parte3 = Bluetooth Mate Silver

nets:
  N1: Parte1.D15/RX3, Parte3.VCC
  N2: Parte1.D14/TX3, Parte3.CTS_5V
  N3: Parte1.5V, Parte3.RX_5V
  N4: Parte1.GND, Parte3.TX_5V
  N5: Parte2.B-, M1.pin_2
  N6: Parte2.B+, M1.pin_1
  N7: Parte2.A-, M2.pin_2
  N8: Parte2.A+, M2.pin_1
